# Fritzing sketch v0-0-4 (saved by Fritzing 0.8.3b)
breadboards: 1

parts:
  LED1 = LED - 5mm [color="Red (633nm)" package="5 mm [THT]"]
  R1 = Resistor [tolerance=±5% resistance=10k package=THT]
  R2 = Resistor [tolerance=±5% resistance=330 package=THT]
  S1 = Pushbutton [package="[THT]"]

nets:
  N1: LED1.anode, R2.Pin_0
  N2: R1.Pin_0, S1.Pin_1, S1.Pin_2
  N3: R1.Pin_1, R2.Pin_1
  N4: S1.Pin_3, S1.Pin_4

notes:
  MaKey MaKey Pins
  D14[ ]
  D5[ ]
  GND [ ]
  5V [ ]
